// Logisim project SIGNEXT.circ as structural Verilog: 5 circuits, main circuit IN_DATA
module IN_DATA (
  input  A15,
  input  A14,
  input  A13,
  input  A12,
  input  A11,
  input  A10,
  input  A9,
  input  A8,
  input  A7,
  input  A6,
  input  A5,
  input  A4,
  input  A3,
  input  A2,
  input  A1,
  input  A0,
  input  COUNT16,
  input  WE,
  input  LOAD,
  input  RST,
  output in_in,
  output More_significant_bit_in
);

  wire clock_1_out, multiplexer_1_out, multiplexer_2_out, multiplexer_3_out, multiplexer_4_out,
       multiplexer_5_out, multiplexer_6_out, multiplexer_7_out, multiplexer_8_out, multiplexer_9_out,
       multiplexer_10_out, multiplexer_11_out, multiplexer_12_out, multiplexer_13_out, multiplexer_14_out,
       multiplexer_15_out, multiplexer_16_out, register_1_q, register_2_q, register_3_q, register_4_q,
       register_5_q, register_6_q, register_7_q, register_8_q, register_9_q, register_10_q, register_11_q,
       register_12_q, register_13_q, register_14_q, register_15_q;

  Clock clock_1 (.out(clock_1_out));
  Multiplexer #(.enable("false")) multiplexer_1 (.in1(A15), .out(multiplexer_1_out), .sel(LOAD));  // open: in0
  Register #(.width(1)) register_1 (.D(multiplexer_1_out), .en(WE), .clk(clock_1_out), .Q(register_1_q), .clr(RST));
  Multiplexer #(.enable("false")) multiplexer_2 (.in0(register_1_q), .in1(A14), .out(multiplexer_2_out), .sel(LOAD));
  Register #(.width(1)) register_2 (.D(multiplexer_2_out), .en(WE), .clk(clock_1_out), .Q(register_2_q), .clr(RST));
  Multiplexer #(.enable("false")) multiplexer_3 (.in0(register_2_q), .in1(A13), .out(multiplexer_3_out), .sel(LOAD));
  Register #(.width(1)) register_3 (.D(multiplexer_3_out), .en(WE), .clk(clock_1_out), .Q(register_3_q), .clr(RST));
  Multiplexer #(.enable("false")) multiplexer_4 (.in0(register_3_q), .in1(A12), .out(multiplexer_4_out), .sel(LOAD));
  Multiplexer #(.enable("false")) multiplexer_5 (.in0(register_4_q), .in1(A11), .out(multiplexer_5_out), .sel(LOAD));
  Register #(.width(1)) register_4 (.D(multiplexer_4_out), .en(WE), .clk(clock_1_out), .Q(register_4_q), .clr(RST));
  Register #(.width(1)) register_5 (.D(multiplexer_5_out), .en(WE), .clk(clock_1_out), .Q(register_5_q), .clr(RST));
  Multiplexer #(.enable("false")) multiplexer_6 (.in0(register_5_q), .in1(A10), .out(multiplexer_6_out), .sel(LOAD));
  Register #(.width(1)) register_6 (.D(multiplexer_6_out), .en(WE), .clk(clock_1_out), .Q(register_6_q), .clr(RST));
  Multiplexer #(.enable("false")) multiplexer_7 (.in0(register_6_q), .in1(A9), .out(multiplexer_7_out), .sel(LOAD));
  Register #(.width(1)) register_7 (.D(multiplexer_7_out), .en(WE), .clk(clock_1_out), .Q(register_7_q), .clr(RST));
  Multiplexer #(.enable("false")) multiplexer_8 (.in0(register_7_q), .in1(A8), .out(multiplexer_8_out), .sel(LOAD));
  Register #(.width(1)) register_8 (.D(multiplexer_8_out), .en(WE), .clk(clock_1_out), .Q(register_8_q), .clr(RST));
  Multiplexer #(.enable("false")) multiplexer_9 (.in0(register_8_q), .in1(A7), .out(multiplexer_9_out), .sel(LOAD));
  Register #(.width(1)) register_9 (.D(multiplexer_9_out), .en(WE), .clk(clock_1_out), .Q(register_9_q), .clr(RST));
  Multiplexer #(.enable("false")) multiplexer_10 (.in0(register_9_q), .in1(A6), .out(multiplexer_10_out), .sel(LOAD));
  Register #(.width(1)) register_10 (.D(multiplexer_10_out), .en(WE), .clk(clock_1_out), .Q(register_10_q), .clr(RST));
  Multiplexer #(.enable("false")) multiplexer_11 (.in0(register_10_q), .in1(A5), .out(multiplexer_11_out), .sel(LOAD));
  Multiplexer #(.enable("false")) multiplexer_12 (.in0(register_11_q), .in1(A4), .out(multiplexer_12_out), .sel(LOAD));
  Register #(.width(1)) register_11 (.D(multiplexer_11_out), .en(WE), .clk(clock_1_out), .Q(register_11_q), .clr(RST));
  Register #(.width(1)) register_12 (.D(multiplexer_12_out), .en(WE), .clk(clock_1_out), .Q(register_12_q), .clr(RST));
  Multiplexer #(.enable("false")) multiplexer_13 (.in0(register_12_q), .in1(A3), .out(multiplexer_13_out), .sel(LOAD));
  Register #(.width(1)) register_13 (.D(multiplexer_13_out), .en(WE), .clk(clock_1_out), .Q(register_13_q), .clr(RST));
  Multiplexer #(.enable("false")) multiplexer_14 (.in0(register_13_q), .in1(A2), .out(multiplexer_14_out), .sel(LOAD));
  Register #(.width(1)) register_14 (.D(multiplexer_14_out), .en(WE), .clk(clock_1_out), .Q(register_14_q), .clr(RST));
  Multiplexer #(.enable("false")) multiplexer_15 (.in0(register_14_q), .in1(A1), .out(multiplexer_15_out), .sel(LOAD));
  Register #(.width(1)) register_15 (.D(multiplexer_15_out), .en(WE), .clk(clock_1_out), .Q(register_15_q), .clr(RST));
  Multiplexer #(.enable("false")) multiplexer_16 (.in0(register_15_q), .in1(A0), .out(multiplexer_16_out), .sel(LOAD));
  Register #(.width(1)) register_16 (.D(multiplexer_16_out), .en(WE), .clk(clock_1_out), .Q(in_in), .clr(RST));
  Transistor transistor_1 (.gate(COUNT16));  // open: in, out

  assign More_significant_bit_in = A15;
endmodule

module cclock (
  input  masterclk,
  output DIVclk,
  output COUNT32,
  output COUNT16
);

  wire d_ff_1_q, d_ff_1_qn, d_ff_2_q, d_ff_2_qn, d_ff_3_q, d_ff_3_qn, d_ff_4_q, d_ff_4_qn, d_ff_5_qn,
       not_1_out, not_2_out, not_3_out, not_4_out, not_5_out, not_6_out, not_7_out, undriven;

  D_Flip_Flop d_ff_1 (.D(d_ff_1_qn), .clk(masterclk), .Q(d_ff_1_q), .Qn(d_ff_1_qn), .reset(undriven));  // open: preset
  D_Flip_Flop d_ff_2 (.D(d_ff_2_qn), .clk(d_ff_1_q), .Q(d_ff_2_q), .Qn(d_ff_2_qn), .reset(undriven));  // open: preset
  D_Flip_Flop d_ff_3 (.D(d_ff_3_qn), .clk(d_ff_2_q), .Q(d_ff_3_q), .Qn(d_ff_3_qn), .reset(undriven));  // open: preset
  D_Flip_Flop d_ff_4 (.D(d_ff_4_qn), .clk(d_ff_3_q), .Q(d_ff_4_q), .Qn(d_ff_4_qn), .reset(undriven));  // open: preset
  D_Flip_Flop d_ff_5 (.D(d_ff_5_qn), .clk(d_ff_4_q), .Q(DIVclk), .Qn(d_ff_5_qn), .reset(undriven));  // open: preset
  not not_1 (not_1_out, d_ff_3_qn);
  not not_2 (not_2_out, d_ff_2_qn);
  not not_3 (not_3_out, d_ff_1_qn);
  and and_1 (COUNT16, d_ff_4_qn, not_1_out, not_2_out, not_3_out);
  not not_4 (not_4_out, d_ff_4_qn);
  and and_2 (COUNT32, d_ff_5_qn, not_4_out, not_5_out, not_6_out, not_7_out);
  not not_5 (not_5_out, d_ff_3_qn);
  not not_6 (not_6_out, d_ff_2_qn);
  not not_7 (not_7_out, d_ff_1_qn);
endmodule

module out_circuit (
  input  O31,
  input  in_2,
  input  in_3,
  input  in_4,
  input  in_5,
  input  in_6,
  input  in_7,
  input  in_8,
  input  in_9,
  input  in_10,
  input  in_11,
  input  in_12,
  input  in_13,
  input  in_14,
  input  in_15,
  input  in_16,
  input  in_17,
  input  in_18,
  input  in_19,
  input  in_20,
  input  in_21,
  input  in_22,
  input  in_23,
  input  in_24,
  input  in_25,
  input  in_26,
  input  in_27,
  input  in_28,
  input  in_29,
  input  in_30,
  input  in_31,
  input  O0,
  input  IN_DATA,
  input  WE,
  input  CLK,
  input  RST
);

  Register #(.width(1)) register_1 (.D(IN_DATA), .en(WE), .clk(CLK), .Q(O31), .clr(RST));
  Register #(.width(1)) register_2 (.D(O31), .en(WE), .clk(CLK), .Q(in_2), .clr(RST));
  Register #(.width(1)) register_3 (.D(in_2), .en(WE), .clk(CLK), .Q(in_3), .clr(RST));
  Register #(.width(1)) register_4 (.D(in_3), .en(CLK), .clk(CLK), .Q(in_4), .clr(RST));
  Register #(.width(1)) register_5 (.D(in_4), .en(WE), .clk(CLK), .Q(in_5), .clr(RST));
  Register #(.width(1)) register_6 (.D(in_5), .en(WE), .clk(CLK), .Q(in_6), .clr(RST));
  Register #(.width(1)) register_7 (.D(in_6), .en(WE), .clk(CLK), .Q(in_7), .clr(RST));
  Register #(.width(1)) register_8 (.D(in_7), .en(CLK), .clk(CLK), .Q(in_8), .clr(RST));
  Register #(.width(1)) register_9 (.D(in_8), .en(WE), .clk(CLK), .Q(in_9), .clr(RST));
  Register #(.width(1)) register_10 (.D(in_9), .en(WE), .clk(CLK), .Q(in_10), .clr(RST));
  Register #(.width(1)) register_11 (.D(in_10), .en(WE), .clk(CLK), .Q(in_11), .clr(RST));
  Register #(.width(1)) register_12 (.D(in_11), .en(WE), .clk(CLK), .Q(in_12), .clr(RST));
  Register #(.width(1)) register_13 (.D(in_12), .en(WE), .clk(CLK), .Q(in_13), .clr(RST));
  Register #(.width(1)) register_14 (.D(in_13), .en(WE), .clk(CLK), .Q(in_14), .clr(RST));
  Register #(.width(1)) register_15 (.D(in_14), .en(WE), .clk(CLK), .Q(in_15), .clr(RST));
  Register #(.width(1)) register_16 (.D(in_15), .en(WE), .clk(CLK), .Q(in_16), .clr(RST));
  Register #(.width(1)) register_17 (.D(in_16), .en(WE), .clk(CLK), .Q(in_17), .clr(RST));
  Register #(.width(1)) register_18 (.D(in_17), .en(WE), .clk(CLK), .Q(in_18), .clr(RST));
  Register #(.width(1)) register_19 (.D(in_18), .en(WE), .clk(CLK), .Q(in_19), .clr(RST));
  Register #(.width(1)) register_20 (.D(in_19), .en(WE), .clk(CLK), .Q(in_20), .clr(RST));
  Register #(.width(1)) register_21 (.D(in_20), .en(WE), .clk(CLK), .Q(in_21), .clr(RST));
  Register #(.width(1)) register_22 (.D(in_21), .en(WE), .clk(CLK), .Q(in_22), .clr(RST));
  Register #(.width(1)) register_23 (.D(in_22), .en(WE), .clk(CLK), .Q(in_23), .clr(RST));
  Register #(.width(1)) register_24 (.D(in_23), .en(WE), .clk(CLK), .Q(in_24), .clr(RST));
  Register #(.width(1)) register_25 (.D(in_24), .en(WE), .clk(CLK), .Q(in_25), .clr(RST));
  Register #(.width(1)) register_26 (.D(in_25), .en(WE), .clk(CLK), .Q(in_26), .clr(RST));
  Register #(.width(1)) register_27 (.D(in_26), .en(WE), .clk(CLK), .Q(in_27), .clr(RST));
  Register #(.width(1)) register_28 (.D(in_27), .en(WE), .clk(CLK), .Q(in_28), .clr(RST));
  Register #(.width(1)) register_29 (.D(in_28), .clk(CLK), .Q(in_29), .clr(RST));  // open: en
  Register #(.width(1)) register_30 (.D(in_29), .en(WE), .clk(CLK), .Q(in_30), .clr(RST));
  Register #(.width(1)) register_31 (.D(in_30), .en(WE), .clk(CLK), .Q(in_31), .clr(RST));
  Register #(.width(1)) register_32 (.D(in_31), .en(WE), .clk(CLK), .clr(RST));  // open: Q
endmodule

module xffff (
  input  WE,
  input  CLK,
  input  LOAD,
  input  CLK16,
  input  MORE_SIGNIFICANT_BIT,
  output OUT_MUX
);

  wire multiplexer_1_out, multiplexer_2_out, multiplexer_3_out, multiplexer_4_out, multiplexer_5_out,
       multiplexer_6_out, multiplexer_7_out, multiplexer_8_out, multiplexer_9_out, multiplexer_10_out,
       multiplexer_11_out, multiplexer_12_out, multiplexer_13_out, multiplexer_14_out, multiplexer_15_out,
       multiplexer_16_out, multiplexer_17_out, multiplexer_18_out, multiplexer_19_out, multiplexer_20_out,
       multiplexer_21_out, multiplexer_22_out, multiplexer_23_out, multiplexer_24_out, multiplexer_25_out,
       multiplexer_26_out, multiplexer_27_out, multiplexer_28_out, multiplexer_29_out, multiplexer_30_out,
       multiplexer_31_out, multiplexer_32_out, multiplexer_33_out, register_1_q, register_2_q, register_3_q,
       register_4_q, register_5_q, register_6_q, register_7_q, register_8_q, register_9_q, register_10_q,
       register_11_q, register_12_q, register_13_q, register_14_q, register_15_q, register_16_q,
       register_17_q, register_18_q, register_19_q, register_20_q, register_21_q, register_22_q,
       register_23_q, register_24_q, register_25_q, register_26_q, register_27_q, register_28_q,
       register_29_q, register_30_q, register_31_q, register_32_q, undriven, undriven_2, undriven_3;

  Multiplexer #(.enable("false")) multiplexer_1 (.in1(1'b1), .out(multiplexer_1_out), .sel(LOAD));  // open: in0
  Register #(.width(1)) register_1 (.D(multiplexer_1_out), .en(WE), .clk(CLK), .Q(register_1_q), .clr(undriven));
  Multiplexer #(.enable("false")) multiplexer_2 (.in1(1'b0), .out(multiplexer_2_out), .sel(LOAD));  // open: in0
  Register #(.width(1)) register_2 (.D(multiplexer_2_out), .en(WE), .clk(CLK), .Q(register_2_q), .clr(undriven_3));
  Multiplexer #(.enable("false")) multiplexer_3 (.in0(register_1_q), .in1(1'b1), .out(multiplexer_3_out), .sel(LOAD));
  Register #(.width(1)) register_3 (.D(multiplexer_3_out), .en(WE), .clk(CLK), .Q(register_3_q), .clr(undriven));
  Multiplexer #(.enable("false")) multiplexer_4 (.in0(register_2_q), .in1(1'b0), .out(multiplexer_4_out), .sel(LOAD));
  Register #(.width(1)) register_4 (.D(multiplexer_4_out), .en(WE), .clk(CLK), .Q(register_4_q), .clr(undriven_3));
  Multiplexer #(.enable("false")) multiplexer_5 (.in0(register_3_q), .in1(1'b1), .out(multiplexer_5_out), .sel(LOAD));
  Multiplexer #(.enable("false")) multiplexer_6 (.in0(register_4_q), .in1(1'b0), .out(multiplexer_6_out), .sel(LOAD));
  Multiplexer #(.enable("false")) multiplexer_7 (.in0(register_5_q), .in1(1'b1), .out(multiplexer_7_out), .sel(LOAD));
  Register #(.width(1)) register_5 (.D(multiplexer_5_out), .en(WE), .clk(CLK), .Q(register_5_q), .clr(undriven));
  Register #(.width(1)) register_6 (.D(multiplexer_6_out), .en(WE), .clk(CLK), .Q(register_6_q), .clr(undriven_3));
  Register #(.width(1)) register_7 (.D(multiplexer_7_out), .en(WE), .clk(CLK), .Q(register_7_q), .clr(undriven));
  Multiplexer #(.enable("false")) multiplexer_8 (.in0(register_6_q), .in1(1'b0), .out(multiplexer_8_out), .sel(LOAD));
  Register #(.width(1)) register_8 (.D(multiplexer_8_out), .en(WE), .clk(CLK), .Q(register_8_q), .clr(undriven_3));
  Multiplexer #(.enable("false")) multiplexer_9 (.in0(register_7_q), .in1(1'b1), .out(multiplexer_9_out), .sel(LOAD));
  Register #(.width(1)) register_9 (.D(multiplexer_9_out), .en(WE), .clk(CLK), .Q(register_9_q), .clr(undriven));
  Multiplexer #(.enable("false")) multiplexer_10 (.in0(register_8_q), .in1(1'b0), .out(multiplexer_10_out), .sel(LOAD));
  Register #(.width(1)) register_10 (.D(multiplexer_10_out), .en(WE), .clk(CLK), .Q(register_10_q), .clr(undriven_3));
  Multiplexer #(.enable("false")) multiplexer_11 (.in0(register_9_q), .in1(1'b1), .out(multiplexer_11_out), .sel(LOAD));
  Register #(.width(1)) register_11 (.D(multiplexer_11_out), .en(WE), .clk(CLK), .Q(register_11_q), .clr(undriven));
  Multiplexer #(.enable("false")) multiplexer_12 (
    .in0(register_10_q), .in1(1'b0), .out(multiplexer_12_out), .sel(LOAD));
  Register #(.width(1)) register_12 (.D(multiplexer_12_out), .en(WE), .clk(CLK), .Q(register_12_q), .clr(undriven_3));
  Multiplexer #(.enable("false")) multiplexer_13 (
    .in0(register_11_q), .in1(1'b1), .out(multiplexer_13_out), .sel(LOAD));
  Register #(.width(1)) register_13 (.D(multiplexer_13_out), .en(WE), .clk(CLK), .Q(register_13_q), .clr(undriven));
  Multiplexer #(.enable("false")) multiplexer_14 (
    .in0(register_12_q), .in1(1'b0), .out(multiplexer_14_out), .sel(LOAD));
  Register #(.width(1)) register_14 (.D(multiplexer_14_out), .en(WE), .clk(CLK), .Q(register_14_q), .clr(undriven_3));
  Multiplexer #(.enable("false")) multiplexer_15 (
    .in0(register_13_q), .in1(1'b1), .out(multiplexer_15_out), .sel(LOAD));
  Register #(.width(1)) register_15 (.D(multiplexer_15_out), .en(WE), .clk(CLK), .Q(register_15_q), .clr(undriven));
  Multiplexer #(.enable("false")) multiplexer_16 (
    .in0(register_14_q), .in1(1'b0), .out(multiplexer_16_out), .sel(LOAD));
  Register #(.width(1)) register_16 (.D(multiplexer_16_out), .en(WE), .clk(CLK), .Q(register_16_q), .clr(undriven_3));
  Multiplexer #(.enable("false")) multiplexer_17 (
    .in0(1'b1), .in1(register_15_q), .out(multiplexer_17_out), .sel(LOAD));
  Register #(.width(1)) register_17 (.D(multiplexer_17_out), .en(WE), .clk(CLK), .Q(register_17_q), .clr(undriven));
  Multiplexer #(.enable("false")) multiplexer_18 (
    .in0(1'b0), .in1(register_16_q), .out(multiplexer_18_out), .sel(LOAD));
  Register #(.width(1)) register_18 (.D(multiplexer_18_out), .en(WE), .clk(CLK), .Q(register_18_q), .clr(undriven_3));
  Multiplexer #(.enable("false")) multiplexer_19 (
    .in0(register_17_q), .in1(1'b1), .out(multiplexer_19_out), .sel(LOAD));
  Register #(.width(1)) register_19 (.D(multiplexer_19_out), .en(WE), .clk(CLK), .Q(register_19_q), .clr(undriven));
  Multiplexer #(.enable("false")) multiplexer_20 (
    .in0(register_18_q), .in1(1'b0), .out(multiplexer_20_out), .sel(LOAD));
  Multiplexer #(.enable("false")) multiplexer_21 (
    .in0(register_19_q), .in1(1'b1), .out(multiplexer_21_out), .sel(LOAD));
  Register #(.width(1)) register_20 (.D(multiplexer_20_out), .en(WE), .clk(CLK), .Q(register_20_q), .clr(undriven_3));
  Register #(.width(1)) register_21 (.D(multiplexer_21_out), .en(WE), .clk(CLK), .Q(register_21_q), .clr(undriven));
  Multiplexer #(.enable("false")) multiplexer_22 (
    .in0(register_20_q), .in1(1'b0), .out(multiplexer_22_out), .sel(LOAD));
  Register #(.width(1)) register_22 (.D(multiplexer_22_out), .en(WE), .clk(CLK), .Q(register_22_q), .clr(undriven_3));
  Multiplexer #(.enable("false")) multiplexer_23 (
    .in0(register_21_q), .in1(1'b1), .out(multiplexer_23_out), .sel(LOAD));
  Register #(.width(1)) register_23 (.D(multiplexer_23_out), .en(WE), .clk(CLK), .Q(register_23_q), .clr(undriven));
  Multiplexer #(.enable("false")) multiplexer_24 (
    .in0(register_22_q), .in1(undriven_2), .out(multiplexer_24_out), .sel(LOAD));
  Register #(.width(1)) register_24 (.D(multiplexer_24_out), .en(WE), .clk(CLK), .Q(register_24_q), .clr(undriven_3));
  Multiplexer #(.enable("false")) multiplexer_25 (
    .in0(register_23_q), .in1(1'b1), .out(multiplexer_25_out), .sel(LOAD));
  Register #(.width(1)) register_25 (.D(multiplexer_25_out), .en(WE), .clk(CLK), .Q(register_25_q), .clr(undriven));
  Multiplexer #(.enable("false")) multiplexer_26 (
    .in0(register_24_q), .in1(1'b0), .out(multiplexer_26_out), .sel(LOAD));
  Register #(.width(1)) register_26 (.D(multiplexer_26_out), .en(WE), .clk(CLK), .Q(register_26_q), .clr(undriven_3));
  Multiplexer #(.enable("false")) multiplexer_27 (
    .in0(register_25_q), .in1(1'b1), .out(multiplexer_27_out), .sel(LOAD));
  Register #(.width(1)) register_27 (.D(multiplexer_27_out), .en(WE), .clk(CLK), .Q(register_27_q), .clr(undriven));
  Multiplexer #(.enable("false")) multiplexer_28 (
    .in0(register_26_q), .in1(1'b0), .out(multiplexer_28_out), .sel(LOAD));
  Register #(.width(1)) register_28 (.D(multiplexer_28_out), .en(WE), .clk(CLK), .Q(register_28_q), .clr(undriven_3));
  Multiplexer #(.enable("false")) multiplexer_29 (
    .in0(register_27_q), .in1(1'b1), .out(multiplexer_29_out), .sel(LOAD));
  Register #(.width(1)) register_29 (.D(multiplexer_29_out), .en(WE), .clk(CLK), .Q(register_29_q), .clr(undriven));
  Multiplexer #(.enable("false")) multiplexer_30 (
    .in0(register_28_q), .in1(1'b0), .out(multiplexer_30_out), .sel(LOAD));
  Register #(.width(1)) register_30 (.D(multiplexer_30_out), .en(WE), .clk(CLK), .Q(register_30_q), .clr(undriven_3));
  Multiplexer #(.enable("false")) multiplexer_31 (
    .in0(register_29_q), .in1(1'b1), .out(multiplexer_31_out), .sel(LOAD));
  Register #(.width(1)) register_31 (.D(multiplexer_31_out), .en(WE), .clk(CLK), .Q(register_31_q), .clr(undriven));
  Multiplexer #(.enable("false")) multiplexer_32 (
    .in0(register_30_q), .in1(1'b0), .out(multiplexer_32_out), .sel(LOAD));
  Register #(.width(1)) register_32 (.D(multiplexer_32_out), .en(WE), .clk(CLK), .Q(register_32_q), .clr(undriven_3));
  Multiplexer #(.enable("false")) multiplexer_33 (
    .in0(register_31_q), .in1(register_32_q), .out(multiplexer_33_out), .sel(MORE_SIGNIFICANT_BIT));
  Transistor #(.\type ("n")) transistor_1 (.in(multiplexer_33_out), .out(OUT_MUX), .gate(CLK16));
endmodule

module signext (
  input  in_1,
  input  in_2,
  input  in_3,
  input  in_4,
  input  in_5,
  input  in_6,
  input  in_7,
  input  in_8,
  input  in_9,
  input  in_10,
  input  in_11,
  input  in_12,
  input  in_13,
  input  in_14,
  input  in_15,
  input  in_16,
  input  in_17,
  input  in_18,
  input  in_19,
  input  in_20,
  input  in_21,
  input  in_22,
  input  in_23,
  input  in_24,
  input  in_25,
  input  in_26,
  input  in_27,
  input  in_28,
  input  in_29,
  input  in_30,
  input  in_31,
  input  in_32,
  input  in_33,
  input  in_34,
  input  in_35,
  input  in_36,
  input  in_37,
  input  in_38,
  input  in_39,
  input  in_40,
  input  in_41,
  input  in_42,
  input  in_43,
  input  in_44,
  input  in_45,
  input  in_46,
  input  in_47,
  input  in_48,
  input  in_49,
  input  in_50,
  input  in_51
);

  wire clock_1_out, COUNT16, DIVclk, IN_IN, moore_significant_bit_IN, XFFF_IN;

  Clock clock_1 (.out(clock_1_out));
  cclock cclock_1 (.masterclk(clock_1_out), .DIVclk(DIVclk), .COUNT16(COUNT16));  // open: COUNT32
  IN_DATA in_data_1 (
    .A15(in_7), .A14(in_9), .A13(in_11), .A12(in_13), .A11(in_15), .A10(in_17), .A9(in_19), .A8(in_21),
    .A7(in_23), .A6(in_25), .A5(in_27), .A4(in_29), .A3(in_31), .A2(in_33), .A1(in_35), .A0(in_37),
    .COUNT16(COUNT16), .WE(DIVclk), .LOAD(in_49), .RST(in_50), .in_in(IN_IN),
    .More_significant_bit_in(moore_significant_bit_IN));
  xffff xffff_1 (
    .WE(in_49), .CLK(DIVclk), .LOAD(in_50), .CLK16(COUNT16), .MORE_SIGNIFICANT_BIT(moore_significant_bit_IN),
    .OUT_MUX(XFFF_IN));
  out_circuit out_circuit_1 (
    .O31(in_1), .in_2(in_2), .in_3(in_3), .in_4(in_4), .in_5(in_5), .in_6(in_6), .in_7(in_8), .in_8(in_10),
    .in_9(in_12), .in_10(in_14), .in_11(in_16), .in_12(in_18), .in_13(in_20), .in_14(in_22), .in_15(in_24),
    .in_16(in_26), .in_17(in_28), .in_18(in_30), .in_19(in_32), .in_20(in_34), .in_21(in_36), .in_22(in_38),
    .in_23(in_39), .in_24(in_40), .in_25(in_41), .in_26(in_42), .in_27(in_43), .in_28(in_44), .in_29(in_45),
    .in_30(in_46), .in_31(in_47), .O0(in_48), .IN_DATA(IN_IN), .WE(in_49), .CLK(DIVclk), .RST(in_51));

  // Other names for the same wires on the sheet: LOAD = in_50; RST = in_51; WE = in_49
endmodule
