// Logisim project SPI.circ as structural Verilog: 5 circuits, main circuit SPI
module SPI (
  input  A7,
  input  A6,
  input  A5,
  input  A4,
  input  A3,
  input  A2,
  input  A1,
  input  A0,
  input  ENABLE_CLK,
  input  in_10,
  input  MCLK,
  input  WE,
  input  LOAD,
  input  RST,
  output B7,
  output B6,
  output B5,
  output B4,
  output B3,
  output B2,
  output B1,
  output B0,
  output READY
);

  wire and_1_out, d_ff_1_q, d_ff_1_qn, d_ff_2_q, d_ff_2_qn, d_ff_3_q, d_ff_3_qn, d_ff_4_q, d_ff_4_qn,
       d_ff_5_q, d_ff_5_qn, d_ff_6_q, d_ff_6_qn, d_ff_7_q, d_ff_7_qn, d_ff_8_qn, multiplexer_1_out,
       multiplexer_2_out, multiplexer_3_out, multiplexer_4_out, multiplexer_5_out, multiplexer_6_out,
       multiplexer_7_out, multiplexer_8_out, multiplexer_9_out, not_1_out, register_2_q, register_3_q,
       register_6_q, register_8_q, register_10_q, register_11_q, register_14_q, register_16_q, register_17_q,
       register_18_q, register_19_q, register_20_q, register_21_q, register_22_q, register_23_q,
       register_24_q, register_25_q, register_26_q, register_27_q, register_28_q, register_29_q,
       register_30_q, register_31_q, register_32_q, transistor_1_out, transistor_2_out, transistor_3_out;

  D_Flip_Flop d_ff_1 (
    .D(d_ff_1_qn), .clk(transistor_1_out), .Q(d_ff_1_q), .Qn(d_ff_1_qn), .reset(RST));  // open: preset
  D_Flip_Flop d_ff_2 (.D(d_ff_2_qn), .clk(d_ff_1_q), .Q(d_ff_2_q), .Qn(d_ff_2_qn), .reset(RST));  // open: preset
  D_Flip_Flop d_ff_3 (.D(d_ff_3_qn), .clk(MCLK), .Q(d_ff_3_q), .Qn(d_ff_3_qn), .reset(RST));  // open: preset
  D_Flip_Flop d_ff_4 (.D(d_ff_4_qn), .clk(d_ff_3_q), .Q(d_ff_4_q), .Qn(d_ff_4_qn), .reset(RST));  // open: preset
  D_Flip_Flop d_ff_5 (.D(d_ff_5_qn), .clk(d_ff_2_q), .Q(d_ff_5_q), .Qn(d_ff_5_qn), .reset(RST));  // open: preset
  D_Flip_Flop d_ff_6 (.D(d_ff_6_qn), .clk(d_ff_4_q), .Q(d_ff_6_q), .Qn(d_ff_6_qn), .reset(RST));  // open: preset
  not not_1 (not_1_out, LOAD);
  Transistor #(.\type ("n")) transistor_1 (.in(transistor_3_out), .out(transistor_1_out), .gate(not_1_out));
  D_Flip_Flop d_ff_7 (.D(d_ff_7_qn), .clk(d_ff_5_q), .Q(d_ff_7_q), .Qn(d_ff_7_qn), .reset(RST));  // open: preset
  Transistor #(.\type ("n")) transistor_2 (.in(d_ff_6_q), .out(transistor_2_out), .gate(ENABLE_CLK));
  D_Flip_Flop d_ff_8 (.D(d_ff_8_qn), .clk(d_ff_7_q), .Qn(d_ff_8_qn), .reset(RST));  // open: Q, preset
  Multiplexer #(.enable("false")) multiplexer_1 (.in0(transistor_2_out), .in1(WE), .out(multiplexer_1_out), .sel(LOAD));
  and and_1 (and_1_out, multiplexer_1_out, transistor_2_out);
  Transistor #(.\type ("n")) transistor_3 (.in(and_1_out), .out(transistor_3_out), .gate(in_10));
  and and_2 (READY, d_ff_8_qn, d_ff_7_qn);
  Register #(.width(1)) register_1 (.D(register_32_q), .en(WE), .clk(transistor_3_out), .Q(B7), .clr(RST));
  Multiplexer #(.enable("false")) multiplexer_2 (.in1(A7), .out(multiplexer_2_out), .sel(LOAD));  // open: in0
  Register #(.width(1)) register_2 (
    .D(multiplexer_2_out), .en(WE), .clk(transistor_3_out), .Q(register_2_q), .clr(RST));
  Multiplexer #(.enable("false")) multiplexer_3 (.in0(register_2_q), .in1(A6), .out(multiplexer_3_out), .sel(LOAD));
  Register #(.width(1)) register_3 (
    .D(multiplexer_3_out), .en(WE), .clk(transistor_3_out), .Q(register_3_q), .clr(RST));
  Register #(.width(1)) register_4 (.D(B7), .en(WE), .clk(transistor_3_out), .Q(B6), .clr(RST));
  Multiplexer #(.enable("false")) multiplexer_4 (.in0(register_3_q), .in1(A5), .out(multiplexer_4_out), .sel(LOAD));
  Register #(.width(1)) register_5 (.D(B6), .en(WE), .clk(transistor_3_out), .Q(B5), .clr(RST));
  Register #(.width(1)) register_6 (
    .D(multiplexer_4_out), .en(WE), .clk(transistor_3_out), .Q(register_6_q), .clr(RST));
  Register #(.width(1)) register_7 (.D(B5), .en(WE), .clk(transistor_3_out), .Q(B4), .clr(RST));
  Multiplexer #(.enable("false")) multiplexer_5 (.in0(register_6_q), .in1(A4), .out(multiplexer_5_out), .sel(LOAD));
  Register #(.width(1)) register_8 (
    .D(multiplexer_5_out), .en(WE), .clk(transistor_3_out), .Q(register_8_q), .clr(RST));
  Register #(.width(1)) register_9 (.D(B4), .en(WE), .clk(transistor_3_out), .Q(B3), .clr(RST));
  Multiplexer #(.enable("false")) multiplexer_6 (.in0(register_8_q), .in1(A3), .out(multiplexer_6_out), .sel(LOAD));
  Register #(.width(1)) register_10 (
    .D(multiplexer_6_out), .en(WE), .clk(transistor_3_out), .Q(register_10_q), .clr(RST));
  Multiplexer #(.enable("false")) multiplexer_7 (.in0(register_10_q), .in1(A2), .out(multiplexer_7_out), .sel(LOAD));
  Register #(.width(1)) register_11 (
    .D(multiplexer_7_out), .en(WE), .clk(transistor_3_out), .Q(register_11_q), .clr(RST));
  Register #(.width(1)) register_12 (.D(B3), .en(WE), .clk(transistor_3_out), .Q(B2), .clr(RST));
  Multiplexer #(.enable("false")) multiplexer_8 (.in0(register_11_q), .in1(A1), .out(multiplexer_8_out), .sel(LOAD));
  Register #(.width(1)) register_13 (.D(B2), .en(WE), .clk(transistor_3_out), .Q(B1), .clr(RST));
  Register #(.width(1)) register_14 (
    .D(multiplexer_8_out), .en(WE), .clk(transistor_3_out), .Q(register_14_q), .clr(RST));
  Register #(.width(1)) register_15 (.D(B1), .en(WE), .clk(transistor_3_out), .Q(B0), .clr(RST));
  Multiplexer #(.enable("false")) multiplexer_9 (.in0(register_14_q), .in1(A0), .out(multiplexer_9_out), .sel(LOAD));
  Register #(.width(1)) register_16 (
    .D(multiplexer_9_out), .en(WE), .clk(transistor_3_out), .Q(register_16_q), .clr(RST));
  Register #(.width(1)) register_17 (.D(register_16_q), .en(WE), .clk(transistor_3_out), .Q(register_17_q), .clr(RST));
  Register #(.width(1)) register_18 (.D(register_31_q), .en(WE), .clk(transistor_3_out), .Q(register_18_q), .clr(RST));
  Register #(.width(1)) register_19 (.D(register_17_q), .en(WE), .clk(transistor_3_out), .Q(register_19_q), .clr(RST));
  Register #(.width(1)) register_20 (.D(register_18_q), .en(WE), .clk(transistor_3_out), .Q(register_20_q), .clr(RST));
  Register #(.width(1)) register_21 (.D(register_19_q), .en(WE), .clk(transistor_3_out), .Q(register_21_q), .clr(RST));
  Register #(.width(1)) register_22 (.D(register_20_q), .en(WE), .clk(transistor_3_out), .Q(register_22_q), .clr(RST));
  Register #(.width(1)) register_23 (.D(register_21_q), .en(WE), .clk(transistor_3_out), .Q(register_23_q), .clr(RST));
  Register #(.width(1)) register_24 (.D(register_22_q), .en(WE), .clk(transistor_3_out), .Q(register_24_q), .clr(RST));
  Register #(.width(1)) register_25 (.D(register_23_q), .en(WE), .clk(transistor_3_out), .Q(register_25_q), .clr(RST));
  Register #(.width(1)) register_26 (.D(register_24_q), .en(WE), .clk(transistor_3_out), .Q(register_26_q), .clr(RST));
  Register #(.width(1)) register_27 (.D(register_25_q), .en(WE), .clk(transistor_3_out), .Q(register_27_q), .clr(RST));
  Register #(.width(1)) register_28 (.D(register_26_q), .en(WE), .clk(transistor_3_out), .Q(register_28_q), .clr(RST));
  Register #(.width(1)) register_29 (.D(register_27_q), .en(WE), .clk(transistor_3_out), .Q(register_29_q), .clr(RST));
  Register #(.width(1)) register_30 (.D(register_28_q), .en(WE), .clk(transistor_3_out), .Q(register_30_q), .clr(RST));
  Register #(.width(1)) register_31 (.D(register_29_q), .en(WE), .clk(transistor_3_out), .Q(register_31_q), .clr(RST));
  Register #(.width(1)) register_32 (.D(register_30_q), .en(WE), .clk(transistor_3_out), .Q(register_32_q), .clr(RST));
endmodule

module MODULO_SPI (
  input  in_1,
  input  in_2,
  input  in_3,
  input  in_4,
  input  in_5,
  input  in_6,
  input  in_7,
  input  in_8,
  input  in_9,
  input  in_10,
  input  in_11,
  input  in_12,
  input  in_13,
  output out_14,
  output out_15,
  output out_16,
  output out_17,
  output out_18,
  output out_19,
  output out_20,
  output out_21,
  output out_22
);

  wire clock_1_out;

  Clock clock_1 (.out(clock_1_out));
  SPI spi_1 (
    .A7(in_1), .A6(in_2), .A5(in_3), .A4(in_4), .A3(in_5), .A2(in_6), .A1(in_7), .A0(in_8),
    .ENABLE_CLK(in_9), .in_10(in_10), .MCLK(clock_1_out), .WE(in_11), .LOAD(in_12), .RST(in_13), .B7(out_14),
    .B6(out_15), .B5(out_16), .B4(out_17), .B3(out_18), .B2(out_19), .B1(out_20), .B0(out_21), .READY(out_22));
endmodule

module Int_logic (
  input  S1,
  input  S2,
  input  WE,
  input  LOAD,
  input  CLK_ENABLE,
  output S_1,
  output S_0
);

  wire and_2_out, not_1_out, not_2_out;

  not not_1 (not_1_out, LOAD);
  not not_2 (not_2_out, S2);
  and and_1 (S_1, WE, not_1_out, CLK_ENABLE);
  and and_2 (and_2_out, not_2_out, CLK_ENABLE);
  or or_1 (S_0, and_2_out, LOAD, S1);
endmodule

module Out_logic (
  input  S1,
  input  S0,
  output RDY
);

  wire and_1_out, and_2_out, not_1_out, not_2_out;

  not not_1 (not_1_out, S1);
  not not_2 (not_2_out, S0);
  and and_1 (and_1_out, not_1_out, not_2_out);
  and and_2 (and_2_out, S1, S0);
  or or_1 (RDY, and_1_out, and_2_out);
endmodule

module STATE_MACHINE (
  input  in_1,
  input  in_2,
  input  in_3,
  input  in_4,
  input  in_5,
  input  in_6,
  input  in_7,
  output out_8
);

  wire clock_1_out, int_logic_1_s_0, int_logic_1_s_1, register_1_q, register_2_q;

  Clock clock_1 (.out(clock_1_out));
  Int_logic int_logic_1 (
    .S1(in_2), .S2(in_3), .WE(in_4), .LOAD(in_5), .CLK_ENABLE(in_6), .S_1(int_logic_1_s_1),
    .S_0(int_logic_1_s_0));
  Register #(.width(1)) register_1 (.D(int_logic_1_s_1), .en(in_1), .clk(clock_1_out), .Q(register_1_q), .clr(in_7));
  Register #(.width(1)) register_2 (.D(int_logic_1_s_0), .en(in_1), .clk(clock_1_out), .Q(register_2_q), .clr(in_7));
  Out_logic out_logic_1 (.S1(register_1_q), .S0(register_2_q), .RDY(out_8));
endmodule
